# Fritzing sketch Lampadina Stampante 3D (saved by Fritzing 0.9.3b)
breadboards: 1

parts:
  Raspberry_Pi_1 = Raspberry Pi 3 [part_number=RPI-3-V1.2]
  KY-1 = keyes
  LED1 = LED - 5mm [color="White (6500K)" package="5 mm [THT]"]
  LED2 = LED - 5mm [color="White (6500K)" package="5 mm [THT]"]
  LED3 = LED - 5mm [color="White (6500K)" package="5 mm [THT]"]
  LED4 = LED - 5mm [color="White (6500K)" package="5 mm [THT]"]
  LED5 = LED - 5mm [color="White (6500K)" package="5 mm [THT]"]
  R1 = Resistor [tolerance=±5% resistance=10 package=THT]

nets:
  N1: Raspberry_Pi_1.GIPO4, KY-1.connector0
  N2: Raspberry_Pi_1.GND, KY-1.connector2, KY-1.connector4
  N3: Raspberry_Pi_1.5V, KY-1.connector1, R1.Pin_0
  N4: KY-1.connector5, LED1.cathode, LED2.cathode, LED3.cathode, LED4.cathode, LED5.cathode
  N5: LED1.anode, LED2.anode, LED3.anode, LED4.anode, LED5.anode, R1.Pin_1
